# Fritzing sketch esp (saved by Fritzing 0.9.3b)
breadboards: 1

parts:
  U2 = V_REG_LD1117VXX [package=78xxl]
  C4 = Electrolytic Capacitor [capacitance=22µF package="1010 [SMD, electrolytic]"]
  U1 = ESP8266 WiFi Module [part_number=ESP8266]
  LED1 = RGB LED (com. anode, rbg) [package="5 mm [THT]"]
  R1 = Resistor [tolerance=±5% resistance=220 package="2010 [SMD]"]
  S2 = Pushbutton [package=THT]
  VCC1 = 4 x AAA Battery Mount
  Composant1 = FTDI Basic Programmer

nets:
  N1: U2.OUT, C4.+, U1.VCC, U1.GPIO_2, U1.ADC_0
  GND: U2.GND, C4.-, U1.GND, U1.GPIO_15, R1.Pin_1, VCC1.-, Composant1.GND
  N2: U2.IN, S2.leg1
  N3: U1.RXD, Composant1.TXO
  N4: U1.TXD, Composant1.RXI
  N5: U1.GPIO_14, LED1.green_cathode
  N6: U1.GPIO_12, LED1.common_anode
  N7: U1.GPIO_13, LED1.red_cathode
  N8: LED1.blue_cathode, R1.Pin_0
  N9: S2.leg0, VCC1.+

notes:
  to GND for flash mode
