# Fritzing sketch esp_strip (saved by Fritzing 0.9.3b)
stripboards: 1

parts:
  S2 = Pushbutton [package=THT]
  U3 = ESP8266 WiFi Module [part_number=ESP8266]
  U4 = V_REG_LD1117VXX [package=78xxl]
  LED2 = RGB LED (com. anode, rbg) [package="5 mm [THT]"]
  VCC2 = 4 x AAA Battery Mount
  Composant2 = FTDI Basic Programmer
  C4 = Electrolytic Capacitor [capacitance=22µF package="1010 [SMD, electrolytic]"]
  R2 = Resistor [tolerance=±5% resistance=220 package="2010 [SMD]"]
  J1 = male pin header, 1 pin [form="♂ (male)"]

nets:
  N1: S2.leg0, U4.GND
  N2: S2.leg1, VCC2.+
  N3: U3.RXD, Composant2.TXO
  N4: U3.VCC, U3.GPIO_2, U3.ADC_0, U4.OUT, C4.+
  N5: U3.GPIO_0, U3.GND, U3.GPIO_15, U4.IN, VCC2.-, C4.-, R2.Pin_0, J1.pin1
  N6: U3.TXD, Composant2.RXI
  N7: U3.GPIO_14, LED2.red_cathode
  N8: U3.GPIO_12, LED2.blue_cathode
  N9: U3.GPIO_13, LED2.green_cathode
  N10: LED2.common_anode, R2.Pin_1

notes:
  ftdi and ground only required for reflash
